# Fritzing sketch gym_timer (saved by Fritzing 0.9.3b)
breadboards: 1

parts:
  Raspberry_Pi_Zero1 = Raspberry Pi Zero
  S1 = Pushbutton [package="[THT]"]
  U1 = 74AHCT125 [part_number=SN74AHCT125 package=dil14]
  R1 = Resistor [tolerance=±5% resistance=330 package=THT]
  Part1 = Audio FX Sound Board + 2x2W Amp
  Power_plug1 = Power plug
  C1 = Electrolytic Capacitor [capacitance=1µF package="100 mil [THT, electrolytic]"]
  U2 = Hirose DF13 Series Header [part_number=DF13#-3P-1.25V package=DF13C-3P-1.25V]

nets:
  3V3: Raspberry_Pi_Zero1.3v3, Raspberry_Pi_Zero1.3V3, S1.Pin_3, S1.Pin_4
  GND: Raspberry_Pi_Zero1.GND, U1.1OE, U1.GND, Part1.GND, Part1.UG, Power_plug1.GND, C1.-, U2.3
  N1: Raspberry_Pi_Zero1.GIPO24, R1.Pin_1
  N2: Raspberry_Pi_Zero1.GIPO23, Part1.RST
  N3: Raspberry_Pi_Zero1.GIPO18, U1.1A
  N4: Raspberry_Pi_Zero1.GIPO15, Part1.TX
  N5: Raspberry_Pi_Zero1.GIPO14, Part1.RX
  N6: S1.Pin_1, S1.Pin_2, R1.Pin_0
  N7: U1.1Y, U2.2
  VCC: U1.VCC, Part1.VIN, Power_plug1.VCC, C1.+, U2.1

custom parts:
  74AHCT125: Quad Level-Shifter (3V to 5V) Quadruple Bus Buffer Gates With 3-State Outputs
  Audio FX Sound Board + 2x2W Amp: The Adafruit Sound Board, the fastest way to add audio effects to a project!
